# Fritzing sketch Stepper.Charger (saved by Fritzing 0.9.4)
breadboards: 1

parts:
  C1 = Capacitor Polarized [package=panasonic_d]
  IC1 = Voltage Regulator [package=78xxl]
  M1 = Stepper Motor - Bipolar  # not connected
  Part1 = Adafruit Micro USB Breakout [part_number="Adafruit #1833"]

nets:
  N1: C1.+, IC1.IN
  GND: C1.-, IC1.GND, Part1.GND
  N2: IC1.OUT, Part1.VBUS

notes:
  <== Here we would have the rectifier bridge, like a KBP307 L, KBP 307 IC, etc.
  Two internal pins: AC.
  Capacitor, 1000uF, 25V
  Regulated 5V output
  Voltage Regulator, 5V out.

custom parts:
  Adafruit Micro USB Breakout: Simple but effective - this breakout board has a USB Micro-B connector, with all 5 pins broken out. Great for pairing with a microcontroller with USB support, or adding USB 5V power to a project. We use a micro-AB connector with through-hole shielding pads for an excellent strong connection - it won't rip off by accident! Comes with one fully assembled and tested micro B breakout PCB and a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
